# Fritzing sketch Šematik projekta (saved by Fritzing 0.9.3b)
breadboards: 1

parts:
  Part1 = Arduino Uno (Rev3)
  J1 = Basic Servo
  J2 = Basic Servo
  Mod1 = KY-008 Laser Transmitter Module [package="Breakout board"]
  Mod2 = KY-023 Dual Axis Joystick Module [package="Breakout board"]

nets:
  N1: Part1.A0, Mod2.VRx
  N2: Part1.A1, Mod2.VRy
  N3: Part1.D8, J2.pulse
  N4: Part1.D9_PWM, J1.pulse
  N5: Part1.D10_PWM/SS, Mod1.S
  N6: Part1.D7, Mod2.SW
  VCC: Part1.5V, J1.vcc, J2.vcc, Mod1.-
  GND: Part1.GND, J1.gnd, J2.gnd, Mod2.GND

notes:
  Y servo motor
  X servo motor
  laser modul
  džojstik

custom parts:
  KY-008 Laser Transmitter Module: KY-008 Laser Transmitter Module, emits a dot shaped red laser beam.
  KY-023 Dual Axis Joystick Module: KY-023 Dual-Axis Joystick Module.
